// Logisim project OPU.circ as structural Verilog: 7 circuits, main circuit main
module main (
);

  wire clock_1_out, controlunit_1_aluop, controlunit_1_alusrc, controlunit_1_linkreg, controlunit_1_memread,
       controlunit_1_memtoreg, controlunit_1_memwrite, controlunit_1_regtoloc, controlunit_1_regwrite;
  wire [1:0] instructionsplitter_1_rd_rt, instructionsplitter_1_rm, instructionsplitter_1_rn,
       multiplexer_1_out;
  wire [3:0] multiplexer_2_out, multiplexer_2_out_2, multiplexer_3_out, multiplexer_3_out_2;
  wire [7:0] adder_1_out, alu_1_aluout, datamemory_1_readdatam, instructionsplitter_1_imm8,
       multiplexer_4_out, PC_q, registerfile_1_readdata1, registerfile_1_readdata2;
  wire [11:0] instructionsplitter_1_opcode;
  wire [23:0] InstructionMemory_dout;

  Clock clock_1 (.out(clock_1_out));
  Adder adder_1 (.a(PC_q), .b(8'h1), .out(adder_1_out));  // open: cin, cout
  Register PC (.D(adder_1_out), .en(1'b1), .clk(clock_1_out), .Q(PC_q));  // open: clr
  RAM #(.dataWidth(24)) InstructionMemory (
    .addr(PC_q), .we(1'b0), .oe(1'b1), .clk(clock_1_out), .dout(InstructionMemory_dout));  // open: din
  InstructionSplitter instructionsplitter_1 (
    .Instruction(InstructionMemory_dout), .Rd_Rt(instructionsplitter_1_rd_rt), .Rn(instructionsplitter_1_rn),
    .Rm(instructionsplitter_1_rm), .imm8(instructionsplitter_1_imm8), .opcode(instructionsplitter_1_opcode));
  ControlUnit controlunit_1 (
    .opcode(instructionsplitter_1_opcode), .MemRead(controlunit_1_memread),
    .MemWrite(controlunit_1_memwrite), .ALUsrc(controlunit_1_alusrc), .ALUOp(controlunit_1_aluop),
    .RegWrite(controlunit_1_regwrite), .RegToLoc(controlunit_1_regtoloc), .MemToReg(controlunit_1_memtoreg),
    .LinkReg(controlunit_1_linkreg));
  Multiplexer #(.width(2)) multiplexer_1 (
    .in0(instructionsplitter_1_rm), .in1(instructionsplitter_1_rd_rt), .out(multiplexer_1_out),
    .sel(controlunit_1_regtoloc));
  Hex_Digit_Display hex_digit_display_1 (.value(registerfile_1_readdata1[7:4]));  // open: dp
  RegisterFile registerfile_1 (
    .C(clock_1_out), .WriteReg(instructionsplitter_1_rd_rt),
    .RegDataW({multiplexer_3_out_2, multiplexer_3_out}), .ReadReg1(instructionsplitter_1_rn),
    .RegWrite(controlunit_1_regwrite), .ReadReg2(multiplexer_1_out), .ReadData1(registerfile_1_readdata1),
    .ReadData2(registerfile_1_readdata2));
  Hex_Digit_Display hex_digit_display_2 (.value(registerfile_1_readdata1[3:0]));  // open: dp
  Multiplexer #(.width(8)) multiplexer_2 (
    .in0(registerfile_1_readdata2), .in1(instructionsplitter_1_imm8),
    .out({multiplexer_2_out_2, multiplexer_2_out}), .sel(controlunit_1_alusrc));
  Hex_Digit_Display hex_digit_display_3 (.value(multiplexer_2_out_2));  // open: dp
  Hex_Digit_Display hex_digit_display_4 (.value(multiplexer_2_out));  // open: dp
  Multiplexer #(.width(8)) multiplexer_3 (
    .in0(multiplexer_4_out), .out({multiplexer_3_out_2, multiplexer_3_out}), .sel(controlunit_1_linkreg));  // open: in1
  Multiplexer #(.width(8)) multiplexer_4 (
    .in0(alu_1_aluout), .in1(datamemory_1_readdatam), .out(multiplexer_4_out), .sel(controlunit_1_memtoreg));
  Hex_Digit_Display hex_digit_display_5 (.value(multiplexer_3_out_2));  // open: dp
  Hex_Digit_Display hex_digit_display_6 (.value(multiplexer_3_out));  // open: dp
  ALU alu_1 (
    .inputA(registerfile_1_readdata1), .inputB({multiplexer_2_out_2, multiplexer_2_out}),
    .ALUOp(controlunit_1_aluop), .ALUOut(alu_1_aluout));
  DataMemory datamemory_1 (
    .C(clock_1_out), .Address(alu_1_aluout), .MemWrite(controlunit_1_memwrite),
    .MemRead(controlunit_1_memread), .WriteDataM(registerfile_1_readdata2), .ReadDataM(datamemory_1_readdatam));

  // Notes on the sheet:
  //   Instruction Memory
  //   inputA
  //   inputB
  //   output
  //   OPU DISPLAY
  //   OPU
  //   (Ouckah Processing Unit)
endmodule

module RegisterFile (
  input  C,
  input  [1:0] WriteReg,
  input  [7:0] RegDataW,
  input  [1:0] ReadReg1,
  input  RegWrite,
  input  [1:0] ReadReg2,
  output [7:0] ReadData1,
  output [7:0] ReadData2
);

  wire and_1_out, and_2_out, and_3_out, and_4_out, decoder_1_out0, decoder_1_out1, decoder_1_out2,
       decoder_1_out3;
  wire [7:0] O0_q, O1_q, O2_q, OZR_q;

  Decoder #(.select(2)) decoder_1 (
    .out0(decoder_1_out0), .out1(decoder_1_out1), .out2(decoder_1_out2), .out3(decoder_1_out3), .sel(WriteReg));  // open: en
  and and_1 (and_1_out, decoder_1_out0, RegWrite);
  and and_2 (and_2_out, decoder_1_out1, RegWrite);
  and and_3 (and_3_out, decoder_1_out2, RegWrite);
  and and_4 (and_4_out, decoder_1_out3, 1'b0);
  Register O0 (.D(RegDataW), .en(and_1_out), .clk(C), .Q(O0_q));  // open: clr
  Register O1 (.D(RegDataW), .en(and_2_out), .clk(C), .Q(O1_q));  // open: clr
  Register O2 (.D(RegDataW), .en(and_3_out), .clk(C), .Q(O2_q));  // open: clr
  Register OZR (.D(RegDataW), .en(and_4_out), .clk(C), .Q(OZR_q));  // open: clr
  Multiplexer #(.select(2), .width(8)) multiplexer_1 (
    .in0(O0_q), .in1(O1_q), .in2(O2_q), .in3(OZR_q), .out(ReadData1), .sel(ReadReg1));
  Multiplexer #(.select(2), .width(8)) multiplexer_2 (
    .in0(O0_q), .in1(O1_q), .in2(O2_q), .in3(OZR_q), .out(ReadData2), .sel(ReadReg2));
endmodule

module ControlUnit (
  input  [11:0] opcode,
  output MemRead,
  output MemWrite,
  output ALUsrc,
  output ALUOp,
  output RegWrite,
  output RegToLoc,
  output MemToReg,
  output LinkReg
);


  assign ALUOp = opcode[8];
  assign ALUsrc = opcode[9];
  assign LinkReg = opcode[4];
  assign MemRead = opcode[11];
  assign MemToReg = opcode[5];
  assign MemWrite = opcode[10];
  assign RegToLoc = opcode[6];
  assign RegWrite = opcode[7];
endmodule

module InstructionSplitter (
  input  [23:0] Instruction,
  output [1:0] Rd_Rt,
  output [1:0] Rn,
  output [1:0] Rm,
  output [7:0] imm8,
  output [11:0] opcode
);


  assign imm8 = Instruction[11:4];
  assign opcode = Instruction[23:12];
  assign Rd_Rt = Instruction[1:0];
  assign Rm = Instruction[5:4];
  assign Rn = Instruction[3:2];

  // Notes on the sheet:
  //   Instruction Format
  //   0 0 0 0 0 0 0 0 0 0 0 0 0 0 0 0 0 0 0 0 0 0 0 0
  //   [0:1] - Rd / Rt
  //   [2:3] - Rn
  //   [4:11] - 111000 + Rm OR imm8
  //   [12:23] - opcode
  //   ADD X0, X1, 2
  //   Opcode
  //   001010000000
  //   Rm + 111000 / imm8
  //   00000010
  //   Rn
  //   01
  //   Rd / Rt
  //   00
  //   001010000000000000100100
endmodule

module ALU (
  input  [7:0] inputA,
  input  [7:0] inputB,
  input  ALUOp,
  output [7:0] ALUOut
);

  wire [7:0] adder_1_out, subtractor_1_out;

  Adder adder_1 (.a(inputA), .b(inputB), .out(adder_1_out));  // open: cin, cout
  Subtractor subtractor_1 (.a(inputA), .b(inputB), .out(subtractor_1_out));  // open: bin, bout
  Multiplexer #(.width(8)) multiplexer_1 (.in0(adder_1_out), .in1(subtractor_1_out), .out(ALUOut), .sel(ALUOp));
endmodule

module DataMemory (
  input  C,
  input  [7:0] Address,
  input  MemWrite,
  input  MemRead,
  input  [7:0] WriteDataM,
  output [7:0] ReadDataM
);

  wire [7:0] Memory_dout;

  RAM Memory (.addr(Address), .we(MemWrite), .oe(1'b1), .clk(C), .din(WriteDataM), .dout(Memory_dout));
  Multiplexer #(.width(8)) multiplexer_1 (.in0(WriteDataM), .in1(Memory_dout), .out(ReadDataM), .sel(MemRead));
endmodule

module SegmentDecoder (
  input  [7:0] inputA
);
endmodule
